# Fritzing sketch Spiritist Telegraph Room Controller (saved by Fritzing 0.9.9b)
breadboards: 1

parts:
  Argon = Particle Argon
  ANTENNA = Antenna
  RG_encoder1 = SprkFn RG Encoder [package="DIP (Dual Inline) [THT]"]
  Neopixel1 = Adafruit RBG Smart Neopixel [package="DIP (Dual Inline) [THT]"]
  Neopixel2 = Adafruit RBG Smart Neopixel [package="DIP (Dual Inline) [THT]"]
  OLED_I2C1 = OLED 128x64 I2C Monochrome Display
  M1 = BMP280

nets (from the breadboard view):
  3.3V: Argon.3.3V, Neopixel1.+, Neopixel2.+, OLED_I2C1.VDD, M1.VIN
  GND: Argon.GND, RG_encoder1.GND, RG_encoder1.B, Neopixel1.G, Neopixel2.G, OLED_I2C1.GND, M1.GND
  N1: Argon.A1, ANTENNA.antenna_lead
  N2: Argon.A3, RG_encoder1.A
  N3: Argon.A4, RG_encoder1.C
  N4: Argon.SDA, OLED_I2C1.SDA, M1.SDA
  N5: Argon.SCL, OLED_I2C1.SCK, M1.SCL
  N6: Argon.D2, Neopixel1.In
  N7: Argon.D4, RG_encoder1.+G
  N8: Argon.D5, RG_encoder1.+R
  N9: Argon.D6, RG_encoder1.SW
  N10: Neopixel1.O, Neopixel2.In

custom parts:
  Particle Argon: The Argon is a powerful Wi-Fi enabled development board that can act as either a standalone Wi-Fi endpoint or Wi-Fi enabled gateway for Particle Mesh networks. It is based on the Nordic nRF52840 and has built-in battery charging circuitry so it’s easy to connect a Li-Po and deploy your local network in minutes. The Argon is great for connecting existing projects to the Particle Device Cloud or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
  SprkFn RG Encoder: SparkFun RG Rotary Encoder
  BMP280: Temperature Humidity Barometric presure Sensor, I2C
